// Logisim project PC.circ as structural Verilog: 1 circuit, main circuit main
module main (
  input  halt,
  input  clock,
  input  [7:0] jump_target,
  input  jump_enable,
  output [7:0] PC_out,
  output [7:0] PC_out__1
);

  wire not_1_out;
  wire [7:0] multiplexer_1_out;

  not not_1 (not_1_out, halt);
  Multiplexer #(.width(8), .enable("false")) multiplexer_1 (
    .in0(PC_out__1), .in1(jump_target), .out(multiplexer_1_out), .sel(jump_enable));
  Register PC (.D(multiplexer_1_out), .en(not_1_out), .Q(PC_out), .clk(clock));  // open: clr
  Adder adder_1 (.a(PC_out), .b(8'h1), .out(PC_out__1));  // open: cin, cout
endmodule
