// Logisim project alu.circ as structural Verilog: 1 circuit, main circuit main
module main (
  input  [3:0] op,
  input  [7:0] A,
  input  [7:0] B,
  input  carry_in,
  output [7:0] \output ,
  output carry_out
);

  wire adder_1_cout, adder_2_cout, subtractor_1_bout, subtractor_2_bout, subtractor_3_bout, subtractor_4_bout;
  wire [2:0] bitselector_1_out, bitselector_2_out;
  wire [7:0] adder_1_out, adder_2_out, and_1_out, not_1_out, or_1_out, shifter_1_out, shifter_2_out,
       subtractor_1_out, subtractor_2_out, subtractor_3_out, subtractor_4_out;

  Adder adder_1 (.a(A), .b(B), .out(adder_1_out), .cout(adder_1_cout));  // open: cin
  Subtractor subtractor_1 (.a(A), .b(B), .out(subtractor_1_out), .bout(subtractor_1_bout));  // open: bin
  Subtractor subtractor_2 (.a(B), .b(A), .out(subtractor_2_out), .bout(subtractor_2_bout));  // open: bin
  assign and_1_out = A & B;  // AND_Gate and_1, 8 bits wide
  assign or_1_out = A | B;  // OR_Gate or_1, 8 bits wide
  assign not_1_out = ~B;  // NOT_Gate not_1, 8 bits wide
  Adder adder_2 (.a(A), .b(B), .out(adder_2_out), .cin(carry_in), .cout(adder_2_cout));
  Subtractor subtractor_3 (.a(A), .b(B), .out(subtractor_3_out), .bin(carry_in), .bout(subtractor_3_bout));
  Subtractor subtractor_4 (.a(B), .b(A), .out(subtractor_4_out), .bin(carry_in), .bout(subtractor_4_bout));
  BitSelector #(.group(3)) bitselector_1 (.in(B), .out(bitselector_1_out), .sel(2'b00));
  BitSelector #(.group(3)) bitselector_2 (.in(B), .out(bitselector_2_out), .sel(2'b00));
  Shifter shifter_1 (.in(A), .\dist (bitselector_1_out), .out(shifter_1_out));
  Shifter #(.shift("lr")) shifter_2 (.in(A), .\dist (bitselector_2_out), .out(shifter_2_out));
  Multiplexer #(.select(4), .width(8), .enable("false")) multiplexer_1 (
    .in0(adder_1_out), .in1(subtractor_1_out), .in2(subtractor_2_out), .in3(and_1_out), .in4(or_1_out),
    .in5(not_1_out), .in6(adder_2_out), .in7(subtractor_3_out), .in8(subtractor_4_out), .in9(shifter_1_out),
    .in10(shifter_2_out), .out(\output ), .sel(op));  // open: in11, in12, in13, in14, in15
  Multiplexer #(.select(4), .enable("false")) multiplexer_2 (
    .in0(adder_1_cout), .in1(subtractor_1_bout), .in2(subtractor_2_bout), .in3(1'b0), .in4(1'b0), .in5(1'b0),
    .in6(adder_2_cout), .in7(subtractor_3_bout), .in8(subtractor_4_bout), .in9(1'b0), .in10(1'b0),
    .out(carry_out), .sel(op));  // open: in11, in12, in13, in14, in15

  // Notes on the sheet:
  //   Add
  //   Sub
  //   RSB
endmodule
