// Logisim project rdg27_lab6.circ as structural Verilog: 2 circuits, main circuit main
module main (
);

  wire CK, Done, ProdWE, Shift, Start;
  wire [7:0] Multiplier_q, shifter_2_out;
  wire [15:0] adder_1_out, Multiplicand_q, Product_q, shifter_1_out;

  Clock clock_1 (.out(CK));
  Button Go (.out(Start));
  LED u_Done (.in(Done));
  Shifter #(.width(16)) shifter_1 (.in(Multiplicand_q), .\dist (4'b0001), .out(shifter_1_out));
  Register #(.width(16)) Multiplicand (.D(shifter_1_out), .en(Shift), .Q(Multiplicand_q), .clk(CK));  // open: clr
  Register #(.width(16)) Product (.D(adder_1_out), .en(ProdWE), .Q(Product_q), .clk(CK));  // open: clr
  Shifter #(.shift("lr")) shifter_2 (.in(Multiplier_q), .\dist (3'b001), .out(shifter_2_out));
  Adder #(.width(16)) adder_1 (.a(Multiplicand_q), .b(Product_q), .out(adder_1_out));  // open: cin, cout
  Register Multiplier (.D(shifter_2_out), .en(Shift), .Q(Multiplier_q), .clk(CK));  // open: clr
  Multiply_Control multiply_control_1 (
    .MPLSB(Multiplier_q[0]), .Start(Start), .Clock(CK), .Shift(Shift), .ProdWE(ProdWE), .Done(Done));
endmodule

module Multiply_Control (
  input  MPLSB,
  input  Start,
  input  Clock,
  output ProdWE,
  output Shift,
  output Done
);

  wire and_1_out, comparator_1_eq, comparator_1_lt, comparator_3_eq, not_1_out, t_ff_1_q;
  wire [7:0] adder_1_out, and_2_out, register_1_q;

  and and_1 (and_1_out, Clock, t_ff_1_q);
  T_Flip_Flop t_ff_1 (.clk(Clock), .T(Start), .Q(t_ff_1_q), .reset(comparator_3_eq));  // open: Qn, preset, en
  Register register_1 (.D(adder_1_out), .Q(register_1_q), .clk(and_1_out), .clr(comparator_3_eq));  // open: en
  assign and_2_out = adder_1_out & 8'h1;  // AND_Gate and_2, 8 bits wide
  Adder adder_1 (.a(register_1_q), .b(8'h1), .out(adder_1_out));  // open: cin, cout
  and and_3 (ProdWE, MPLSB, comparator_1_lt);
  Comparator comparator_1 (.a(and_2_out), .b(8'h1), .eq(comparator_1_eq), .lt(comparator_1_lt));  // open: gt
  Comparator comparator_2 (.a(adder_1_out), .b(8'h1), .eq(Done));  // open: gt, lt
  Comparator comparator_3 (.a(adder_1_out), .b(8'h10), .eq(comparator_3_eq));  // open: gt, lt
  and and_4 (Shift, comparator_1_eq, not_1_out);
  not not_1 (not_1_out, Done);
endmodule
