// Logisim project registerFile.circ as structural Verilog: 1 circuit, main circuit main
module main (
  input  [7:0] write_bits,
  input  clock,
  input  [2:0] src_reg_index,
  input  [2:0] dest_reg_index,
  input  write_enable,
  output [7:0] src_reg_out,
  output [7:0] src_dest_out
);

  wire demultiplexer_1_out1, demultiplexer_1_out2, demultiplexer_1_out3, demultiplexer_1_out4,
       demultiplexer_1_out5, demultiplexer_1_out6, demultiplexer_1_out7, not_1_out;
  wire [7:0] register_1_q, register_2_q, register_3_q, register_4_q, register_5_q, register_6_q, register_7_q;

  Demultiplexer #(.select(3)) demultiplexer_1 (
    .out1(demultiplexer_1_out1), .out2(demultiplexer_1_out2), .out3(demultiplexer_1_out3),
    .out4(demultiplexer_1_out4), .out5(demultiplexer_1_out5), .out6(demultiplexer_1_out6),
    .out7(demultiplexer_1_out7), .in(1'b1), .sel(dest_reg_index), .en(write_enable));  // open: out0
  not not_1 (not_1_out, write_enable);
  Register register_1 (.D(write_bits), .en(demultiplexer_1_out1), .Q(register_1_q), .clk(clock));  // open: clr
  Register register_2 (.D(write_bits), .en(demultiplexer_1_out2), .Q(register_2_q), .clk(clock));  // open: clr
  Register register_3 (.D(write_bits), .en(demultiplexer_1_out3), .Q(register_3_q), .clk(clock));  // open: clr
  Register register_4 (.D(write_bits), .en(demultiplexer_1_out4), .Q(register_4_q), .clk(clock));  // open: clr
  Register register_5 (.D(write_bits), .en(demultiplexer_1_out5), .Q(register_5_q), .clk(clock));  // open: clr
  Register register_6 (.D(write_bits), .en(demultiplexer_1_out6), .Q(register_6_q), .clk(clock));  // open: clr
  Register register_7 (.D(write_bits), .en(demultiplexer_1_out7), .Q(register_7_q), .clk(clock));  // open: clr
  Multiplexer #(.select(3), .width(8), .enable("false")) multiplexer_1 (
    .in1(register_1_q), .in2(register_2_q), .in3(register_3_q), .in4(register_4_q), .in5(register_5_q),
    .in6(register_6_q), .in7(register_7_q), .out(src_reg_out), .sel(src_reg_index));  // open: in0
  Multiplexer #(.select(3), .width(8)) multiplexer_2 (
    .in1(register_1_q), .in2(register_2_q), .in3(register_3_q), .in4(register_4_q), .in5(register_5_q),
    .in6(register_6_q), .in7(register_7_q), .out(src_dest_out), .sel(dest_reg_index), .en(not_1_out));  // open: in0
endmodule
